// Digital circuit Adaptador.dig as structural Verilog
module Adaptador (
  input  C2_Y,
  input  C2_X,
  input  C2_W,
  input  C2_V,
  input  C2_U,
  input  C2_T,
  input  C2_S,
  input  SiM_Y,
  input  SiM_X,
  input  SiM_W,
  input  SiM_V,
  input  SiM_U,
  input  SiM_T,
  input  SiM_S,
  output Y,
  output X,
  output W,
  output V,
  output U,
  output T,
  output S
);

  xor xor_1 (Y, C2_Y, SiM_Y);
  xor xor_2 (X, C2_X, SiM_X);
  xor xor_3 (W, C2_W, SiM_W);
  xor xor_4 (V, C2_V, SiM_V);
  xor xor_5 (U, C2_U, SiM_U);
  xor xor_6 (T, C2_T, SiM_T);
  xor xor_7 (S, C2_S, SiM_S);
endmodule
