// Digital circuit Controlador.dig as structural Verilog
module Controlador (
  input  Op,
  input  Codi,
  output A_plus_B_C2,
  output A_plus_B_SiM,
  output A_B_C2,
  output A_B_SiM
);

  wire not_1_out, not_2_out;

  not not_1 (not_1_out, Op);
  not not_2 (not_2_out, Codi);
  and and_1 (A_plus_B_C2, not_1_out, not_2_out);
  and and_2 (A_plus_B_SiM, not_1_out, Codi);
  and and_3 (A_B_C2, Op, not_2_out);
  and and_4 (A_B_SiM, Op, Codi);
endmodule
