// Digital circuit ConversorSiMaC2.dig as structural Verilog
module ConversorSiMaC2 (
  input  A2_2,
  input  A1_2,
  input  A0_2,
  output A2,
  output A1,
  output A0
);

  wire and_1_out, and_2_out, and_3_out, and_4_out, and_5_out, not_1_out, not_2_out, not_3_out;

  not not_1 (not_1_out, A2_2);
  not not_2 (not_2_out, A1_2);
  not not_3 (not_3_out, A0_2);
  and and_1 (and_1_out, A2_2, A1_2);
  and and_2 (and_2_out, A0_2, A2_2);
  and and_3 (and_3_out, A0_2, not_2_out, A2_2);
  and and_4 (and_4_out, not_3_out, A2_2, A1_2);
  and and_5 (and_5_out, A1_2, not_1_out);
  or or_1 (A2, and_1_out, and_2_out);
  or or_2 (A1, and_3_out, and_4_out, and_5_out);

  assign A0 = A0_2;
endmodule
