// Digital circuit Decodificador C2.dig as structural Verilog
module Decodificador_C2 (
  input  A,
  input  B,
  input  C,
  input  E,
  output Y,
  output X,
  output W,
  output V,
  output U,
  output T,
  output S
);

  wire and_1_out, and_2_out, and_3_out, and_4_out, and_5_out, and_6_out, and_7_out, and_8_out, and_9_out,
       and_10_out, and_11_out, and_12_out, and_13_out, and_14_out, not_1_out, not_2_out, not_3_out, or_1_out,
       or_2_out, or_3_out, or_4_out, or_5_out;

  not not_1 (not_1_out, A);
  not not_2 (not_2_out, B);
  not not_3 (not_3_out, C);
  and and_1 (and_1_out, not_1_out, not_3_out);
  and and_2 (and_2_out, not_1_out, B);
  and and_3 (and_3_out, A, not_2_out, C);
  and and_4 (and_4_out, B, not_3_out);
  or or_1 (or_1_out, not_2_out, C);
  and and_5 (and_5_out, not_1_out, not_3_out);
  and and_6 (and_6_out, not_1_out, B);
  and and_7 (and_7_out, A, not_2_out, C);
  and and_8 (and_8_out, B, not_3_out);
  and and_9 (and_9_out, not_1_out, not_3_out);
  and and_10 (and_10_out, B, not_3_out);
  and and_11 (and_11_out, not_2_out, not_3_out);
  and and_12 (and_12_out, not_1_out, B);
  and and_13 (and_13_out, A, not_2_out);
  and and_14 (and_14_out, B, not_3_out);
  or or_2 (or_2_out, and_1_out, and_2_out, and_3_out, and_4_out);
  or or_3 (or_3_out, and_5_out, and_6_out, and_7_out, and_8_out);
  or or_4 (or_4_out, and_9_out, and_10_out);
  or or_5 (or_5_out, and_12_out, and_13_out, and_14_out);
  and and_15 (Y, E, or_2_out);
  and and_16 (X, E, or_1_out);
  and and_17 (W, 1'b1, E);
  and and_18 (V, E, or_3_out);
  and and_19 (U, E, or_4_out);
  and and_20 (T, and_11_out, E);
  and and_21 (S, E, or_5_out);
endmodule
