// Digital circuit Decodificador SiM.dig as structural Verilog
module Decodificador_SiM (
  input  B,
  input  C,
  input  E,
  output Y,
  output X,
  output W,
  output V,
  output U,
  output T,
  output S
);

  wire and_1_out, not_1_out, not_2_out, or_1_out, or_2_out, or_3_out;

  not not_1 (not_1_out, B);
  not not_2 (not_2_out, C);
  or or_1 (or_1_out, B, not_2_out);
  or or_2 (or_2_out, not_1_out, C);
  or or_3 (or_3_out, B, not_2_out);
  and and_1 (and_1_out, not_1_out, not_2_out);
  and and_2 (Y, E, or_1_out);
  and and_3 (X, E, or_2_out);
  and and_4 (W, E, 1'b1);
  and and_5 (V, E, or_3_out);
  and and_6 (U, E, not_2_out);
  and and_7 (T, E, and_1_out);
  and and_8 (S, E, B);
endmodule
