// Digital circuit Enable.dig as structural Verilog
module Enable (
  input  A2_2,
  input  B2_2,
  input  A1_2,
  input  B1_2,
  input  A0_2,
  input  B0_2,
  input  E,
  output A2,
  output B2,
  output A1,
  output B1,
  output A0,
  output B0
);

  and and_1 (A2, A2_2, E);
  and and_2 (B2, B2_2, E);
  and and_3 (A1, A1_2, E);
  and and_4 (B1, B1_2, E);
  and and_5 (A0, A0_2, E);
  and and_6 (B0, B0_2, E);
endmodule
