// Digital circuit Multiplexor.dig as structural Verilog
module Multiplexor (
  input  D0,
  input  D1,
  input  D2,
  input  D3,
  input  S1,
  input  S0,
  output Y
);

  wire and_1_out, and_2_out, and_3_out, and_4_out, not_1_out, not_2_out;

  not not_1 (not_1_out, S1);
  not not_2 (not_2_out, S0);
  and and_1 (and_1_out, S0, S1, D3);
  and and_2 (and_2_out, not_2_out, S1, D2);
  and and_3 (and_3_out, S0, not_1_out, D1);
  and and_4 (and_4_out, not_2_out, not_1_out, D0);
  or or_1 (Y, and_1_out, and_2_out, and_3_out, and_4_out);
endmodule
