// Digital circuit Restador C2.dig as structural Verilog
module Restador_C2 (
  input  A2,
  input  B2,
  input  A1,
  input  B1,
  input  A0,
  input  B0,
  output R2,
  output R1,
  output R0,
  output C,
  output O
);

  wire full_adder_2_c, full_adder_3_c, not_1_out, not_2_out, not_3_out;

  xor xor_1 (O, C, full_adder_2_c);
  not not_1 (not_1_out, B2);
  Full_Adder full_adder_1 (.A(A2), .B(not_1_out), .Cin(full_adder_2_c), .C(C), .S(R2));
  not not_2 (not_2_out, B1);
  Full_Adder full_adder_2 (.A(A1), .B(not_2_out), .Cin(full_adder_3_c), .C(full_adder_2_c), .S(R1));
  not not_3 (not_3_out, B0);
  Full_Adder full_adder_3 (.A(A0), .B(not_3_out), .Cin(1'b1), .C(full_adder_3_c), .S(R0));
endmodule
