// Digital circuit Sumador SiM.dig as structural Verilog
module Sumador_SiM (
  input  A2,
  input  B2,
  input  A1,
  input  B1,
  input  A0,
  input  B0,
  output R2,
  output R1,
  output R0,
  output C,
  output O
);

  wire and_1_out, and_3_out, conversorsimac2_1_a0, conversorsimac2_1_a1, conversorsimac2_1_a2,
       conversorsimac2_2_a0, conversorsimac2_2_a1, conversorsimac2_2_a2, not_1_out, or_3_out, sumadorc2_1_c,
       sumadorc2_1_o, sumadorc2_1_r2;

  ConversorSiMaC2 conversorsimac2_1 (
    .A2_2(A2), .A1_2(A1), .A0_2(A0), .A2(conversorsimac2_1_a2), .A1(conversorsimac2_1_a1),
    .A0(conversorsimac2_1_a0));
  ConversorSiMaC2 conversorsimac2_2 (
    .A2_2(B2), .A1_2(B1), .A0_2(B0), .A2(conversorsimac2_2_a2), .A1(conversorsimac2_2_a1),
    .A0(conversorsimac2_2_a0));
  SumadorC2 sumadorc2_1 (
    .A2(conversorsimac2_1_a2), .B2(conversorsimac2_2_a2), .A1(conversorsimac2_1_a1),
    .B1(conversorsimac2_2_a1), .A0(conversorsimac2_1_a0), .B0(conversorsimac2_2_a0), .R2(sumadorc2_1_r2),
    .R1(R1), .R0(R0), .C(sumadorc2_1_c), .O(sumadorc2_1_o));
  or or_1 (O, and_3_out, sumadorc2_1_o);
  and and_1 (and_1_out, O, sumadorc2_1_c);
  or or_2 (C, and_1_out, sumadorc2_1_o);
  or or_3 (or_3_out, R1, R0);
  and and_2 (R2, sumadorc2_1_r2, or_3_out);
  not not_1 (not_1_out, R2);
  and and_3 (and_3_out, not_1_out, sumadorc2_1_r2);
endmodule
