// Digital circuit Sumador.dig as structural Verilog
module Sumador (
  input  A2,
  input  B2,
  input  A1,
  input  B1,
  input  A0,
  input  B0,
  output R2,
  output R1,
  output R0,
  output C,
  output O
);

  wire half_adder_1_c;

  Full_Adder full_adder_1 (.A(A2), .B(B2), .Cin(O), .C(C), .S(R2));
  Full_Adder full_adder_2 (.A(A1), .B(B1), .Cin(half_adder_1_c), .C(O), .S(R1));
  Half_Adder half_adder_1 (.A(A0), .B(B0), .S(R0), .C(half_adder_1_c));
endmodule
