// Digital circuit SumadorC2.dig as structural Verilog
module SumadorC2 (
  input  A2,
  input  B2,
  input  A1,
  input  B1,
  input  A0,
  input  B0,
  output R2,
  output R1,
  output R0,
  output C,
  output O
);

  wire full_adder_2_c, half_adder_1_c;

  xor xor_1 (O, C, full_adder_2_c);
  Full_Adder full_adder_1 (.A(A2), .B(B2), .Cin(full_adder_2_c), .C(C), .S(R2));
  Full_Adder full_adder_2 (.A(A1), .B(B1), .Cin(half_adder_1_c), .C(full_adder_2_c), .S(R1));
  Half_Adder half_adder_1 (.A(A0), .B(B0), .S(R0), .C(half_adder_1_c));
endmodule
