// Digital circuit arxiu.dig as structural Verilog
module arxiu (
  input  A2,
  input  B2,
  input  A1,
  input  B1,
  input  A0,
  input  B0,
  input  Op,
  input  Codi,
  output R2,
  output R1,
  output R0,
  output O,
  output C
);

  wire _1, _2, _3, _4, _5, _6, _7, _8, _9, _10, _11, _12, _13, _14, _15, _16, _17, _18, _19, _20,
       adaptador_1_s, adaptador_1_t, adaptador_1_u, adaptador_1_v, adaptador_1_w, adaptador_1_x,
       adaptador_1_y, adaptador_2_s, adaptador_2_t, adaptador_2_u, adaptador_2_v, adaptador_2_w,
       adaptador_2_x, adaptador_2_y, adaptador_3_s, adaptador_3_t, adaptador_3_u, adaptador_3_v,
       adaptador_3_w, adaptador_3_x, adaptador_3_y, C2, controlador_1_a_b_c2, controlador_1_a_b_sim,
       controlador_1_a_plus_b_c2, controlador_1_a_plus_b_sim, conversorsimac2_1_a0, conversorsimac2_1_a1,
       conversorsimac2_1_a2, decodificador_c2_1_s, decodificador_c2_1_t, decodificador_c2_1_u,
       decodificador_c2_1_v, decodificador_c2_1_w, decodificador_c2_1_x, decodificador_c2_1_y,
       decodificador_c2_2_s, decodificador_c2_2_t, decodificador_c2_2_u, decodificador_c2_2_v,
       decodificador_c2_2_w, decodificador_c2_2_x, decodificador_c2_2_y, decodificador_c2_3_s,
       decodificador_c2_3_t, decodificador_c2_3_u, decodificador_c2_3_v, decodificador_c2_3_w,
       decodificador_c2_3_x, decodificador_c2_3_y, decodificador_sim_1_s, decodificador_sim_1_t,
       decodificador_sim_1_u, decodificador_sim_1_v, decodificador_sim_1_w, decodificador_sim_1_x,
       decodificador_sim_1_y, decodificador_sim_2_s, decodificador_sim_2_t, decodificador_sim_2_u,
       decodificador_sim_2_v, decodificador_sim_2_w, decodificador_sim_2_x, decodificador_sim_2_y,
       decodificador_sim_3_s, decodificador_sim_3_t, decodificador_sim_3_u, decodificador_sim_3_v,
       decodificador_sim_3_w, decodificador_sim_3_x, decodificador_sim_3_y, enable_1_a0, enable_1_a1,
       enable_1_a2, enable_1_b0, enable_1_b1, enable_1_b2, enable_2_a0, enable_2_a1, enable_2_a2,
       enable_2_b0, enable_2_b1, enable_2_b2, enable_3_a0, enable_3_a1, enable_3_a2, enable_3_b0,
       enable_3_b1, enable_3_b2, enable_4_a0, enable_4_a1, enable_4_a2, enable_4_b0, enable_4_b1,
       enable_4_b2, enable_5_a0, enable_5_a1, enable_5_a2, enable_6_a0, enable_6_a1, enable_6_a2,
       multiplexor_1_y, multiplexor_2_y, multiplexor_3_y, SiM;

  Controlador controlador_1 (
    .Op(Op), .Codi(Codi), .A_plus_B_C2(controlador_1_a_plus_b_c2), .A_plus_B_SiM(controlador_1_a_plus_b_sim),
    .A_B_C2(controlador_1_a_b_c2), .A_B_SiM(controlador_1_a_b_sim));
  Decodificador_C2 decodificador_c2_1 (
    .A(A2), .B(A1), .C(A0), .E(C2), .Y(decodificador_c2_1_y), .X(decodificador_c2_1_x),
    .W(decodificador_c2_1_w), .V(decodificador_c2_1_v), .U(decodificador_c2_1_u), .T(decodificador_c2_1_t),
    .S(decodificador_c2_1_s));
  Decodificador_SiM decodificador_sim_1 (
    .B(A1), .C(A0), .E(SiM), .Y(decodificador_sim_1_y), .X(decodificador_sim_1_x), .W(decodificador_sim_1_w),
    .V(decodificador_sim_1_v), .U(decodificador_sim_1_u), .T(decodificador_sim_1_t), .S(decodificador_sim_1_s));
  Decodificador_C2 decodificador_c2_2 (
    .A(B2), .B(B1), .C(B0), .E(C2), .Y(decodificador_c2_2_y), .X(decodificador_c2_2_x),
    .W(decodificador_c2_2_w), .V(decodificador_c2_2_v), .U(decodificador_c2_2_u), .T(decodificador_c2_2_t),
    .S(decodificador_c2_2_s));
  Decodificador_SiM decodificador_sim_2 (
    .B(B1), .C(B0), .E(SiM), .Y(decodificador_sim_2_y), .X(decodificador_sim_2_x), .W(decodificador_sim_2_w),
    .V(decodificador_sim_2_v), .U(decodificador_sim_2_u), .T(decodificador_sim_2_t), .S(decodificador_sim_2_s));
  Enable enable_1 (
    .A2_2(A2), .B2_2(B2), .A1_2(A1), .B1_2(B1), .A0_2(A0), .B0_2(B0), .E(controlador_1_a_plus_b_c2),
    .A2(enable_1_a2), .B2(enable_1_b2), .A1(enable_1_a1), .B1(enable_1_b1), .A0(enable_1_a0), .B0(enable_1_b0));
  Enable enable_2 (
    .A2_2(A2), .B2_2(B2), .A1_2(A1), .B1_2(B1), .A0_2(A0), .B0_2(B0), .E(controlador_1_a_plus_b_sim),
    .A2(enable_2_a2), .B2(enable_2_b2), .A1(enable_2_a1), .B1(enable_2_b1), .A0(enable_2_a0), .B0(enable_2_b0));
  Enable enable_3 (
    .A2_2(A2), .B2_2(B2), .A1_2(A1), .B1_2(B1), .A0_2(A0), .B0_2(B0), .E(controlador_1_a_b_c2),
    .A2(enable_3_a2), .B2(enable_3_b2), .A1(enable_3_a1), .B1(enable_3_b1), .A0(enable_3_a0), .B0(enable_3_b0));
  Enable enable_4 (
    .A2_2(A2), .B2_2(B2), .A1_2(A1), .B1_2(B1), .A0_2(A0), .B0_2(B0), .E(controlador_1_a_b_sim),
    .A2(enable_4_a2), .B2(enable_4_b2), .A1(enable_4_a1), .B1(enable_4_b1), .A0(enable_4_a0), .B0(enable_4_b0));
  or or_1 (C2, controlador_1_a_plus_b_c2, controlador_1_a_b_c2);
  or or_2 (SiM, controlador_1_a_plus_b_sim, controlador_1_a_b_sim);
  SumadorC2 sumadorc2_1 (
    .A2(enable_1_a2), .B2(enable_1_b2), .A1(enable_1_a1), .B1(enable_1_b1), .A0(enable_1_a0),
    .B0(enable_1_b0), .R2(_1), .R1(_2), .R0(_3), .C(_4), .O(_5));
  Sumador_SiM sumador_sim_1 (
    .A2(enable_2_a2), .B2(enable_2_b2), .A1(enable_2_a1), .B1(enable_2_b1), .A0(enable_2_a0),
    .B0(enable_2_b0), .R2(_6), .R1(_7), .R0(_8), .C(_9), .O(_10));
  Restador_C2 restador_c2_1 (
    .A2(enable_3_a2), .B2(enable_3_b2), .A1(enable_3_a1), .B1(enable_3_b1), .A0(enable_3_a0),
    .B0(enable_3_b0), .R2(_11), .R1(_12), .R0(_13), .C(_14), .O(_15));
  Restador_SiM restador_sim_1 (
    .A2(enable_4_a2), .B2(enable_4_b2), .A1(enable_4_a1), .B1(enable_4_b1), .A0(enable_4_a0),
    .B0(enable_4_b0), .R2(_16), .R1(_17), .R0(_18), .C(_19), .O(_20));
  Adaptador adaptador_1 (
    .C2_Y(decodificador_c2_1_y), .C2_X(decodificador_c2_1_x), .C2_W(decodificador_c2_1_w),
    .C2_V(decodificador_c2_1_v), .C2_U(decodificador_c2_1_u), .C2_T(decodificador_c2_1_t),
    .C2_S(decodificador_c2_1_s), .SiM_Y(decodificador_sim_1_y), .SiM_X(decodificador_sim_1_x),
    .SiM_W(decodificador_sim_1_w), .SiM_V(decodificador_sim_1_v), .SiM_U(decodificador_sim_1_u),
    .SiM_T(decodificador_sim_1_t), .SiM_S(decodificador_sim_1_s), .Y(adaptador_1_y), .X(adaptador_1_x),
    .W(adaptador_1_w), .V(adaptador_1_v), .U(adaptador_1_u), .T(adaptador_1_t), .S(adaptador_1_s));
  Adaptador adaptador_2 (
    .C2_Y(decodificador_c2_2_y), .C2_X(decodificador_c2_2_x), .C2_W(decodificador_c2_2_w),
    .C2_V(decodificador_c2_2_v), .C2_U(decodificador_c2_2_u), .C2_T(decodificador_c2_2_t),
    .C2_S(decodificador_c2_2_s), .SiM_Y(decodificador_sim_2_y), .SiM_X(decodificador_sim_2_x),
    .SiM_W(decodificador_sim_2_w), .SiM_V(decodificador_sim_2_v), .SiM_U(decodificador_sim_2_u),
    .SiM_T(decodificador_sim_2_t), .SiM_S(decodificador_sim_2_s), .Y(adaptador_2_y), .X(adaptador_2_x),
    .W(adaptador_2_w), .V(adaptador_2_v), .U(adaptador_2_u), .T(adaptador_2_t), .S(adaptador_2_s));
  Multiplexor multiplexor_1 (.D0(_1), .D1(_6), .D2(_11), .D3(_16), .S1(Op), .S0(Codi), .Y(multiplexor_1_y));
  Multiplexor multiplexor_2 (.D0(_2), .D1(_7), .D2(_12), .D3(_17), .S1(Op), .S0(Codi), .Y(multiplexor_2_y));
  Multiplexor multiplexor_3 (.D0(_3), .D1(_8), .D2(_13), .D3(_18), .S1(Op), .S0(Codi), .Y(multiplexor_3_y));
  Seven_Seg seven_seg_1 (.a(1'b0), .b(1'b0), .c(1'b0), .d(1'b0), .e(1'b0), .f(1'b0), .g(A2), .dp(1'b0));
  Seven_Seg seven_seg_2 (.a(1'b0), .b(1'b0), .c(1'b0), .d(1'b0), .e(1'b0), .f(1'b0), .g(B2), .dp(1'b0));
  Seven_Seg seven_seg_3 (
    .a(adaptador_1_v), .b(adaptador_1_w), .c(adaptador_1_x), .d(adaptador_1_y), .e(adaptador_1_u),
    .f(adaptador_1_t), .g(adaptador_1_s), .dp(1'b0));
  Seven_Seg seven_seg_4 (
    .a(adaptador_2_v), .b(adaptador_2_w), .c(adaptador_2_x), .d(adaptador_2_y), .e(adaptador_2_u),
    .f(adaptador_2_t), .g(adaptador_2_s), .dp(1'b0));
  Enable enable_5 (
    .A2_2(multiplexor_1_y), .B2_2(1'b0), .A1_2(multiplexor_2_y), .B1_2(1'b0), .A0_2(multiplexor_3_y),
    .B0_2(1'b0), .E(C2), .A2(enable_5_a2), .A1(enable_5_a1), .A0(enable_5_a0));  // open: B2, B1, B0
  Enable enable_6 (
    .A2_2(multiplexor_1_y), .B2_2(1'b0), .A1_2(multiplexor_2_y), .B1_2(1'b0), .A0_2(multiplexor_3_y),
    .B0_2(1'b0), .E(SiM), .A2(enable_6_a2), .A1(enable_6_a1), .A0(enable_6_a0));  // open: B2, B1, B0
  Multiplexor multiplexor_4 (.D0(_4), .D1(_9), .D2(_14), .D3(_19), .S1(Op), .S0(Codi), .Y(C));
  Multiplexor multiplexor_5 (.D0(_5), .D1(_10), .D2(_15), .D3(_20), .S1(Op), .S0(Codi), .Y(O));
  ConversorSiMaC2 conversorsimac2_1 (
    .A2_2(enable_6_a2), .A1_2(enable_6_a1), .A0_2(enable_6_a0), .A2(conversorsimac2_1_a2),
    .A1(conversorsimac2_1_a1), .A0(conversorsimac2_1_a0));
  or or_3 (R2, conversorsimac2_1_a2, enable_5_a2);
  or or_4 (R1, conversorsimac2_1_a1, enable_5_a1);
  or or_5 (R0, conversorsimac2_1_a0, enable_5_a0);
  Decodificador_C2 decodificador_c2_3 (
    .A(R2), .B(R1), .C(R0), .E(C2), .Y(decodificador_c2_3_y), .X(decodificador_c2_3_x),
    .W(decodificador_c2_3_w), .V(decodificador_c2_3_v), .U(decodificador_c2_3_u), .T(decodificador_c2_3_t),
    .S(decodificador_c2_3_s));
  Decodificador_SiM decodificador_sim_3 (
    .B(R1), .C(R0), .E(SiM), .Y(decodificador_sim_3_y), .X(decodificador_sim_3_x), .W(decodificador_sim_3_w),
    .V(decodificador_sim_3_v), .U(decodificador_sim_3_u), .T(decodificador_sim_3_t), .S(decodificador_sim_3_s));
  Adaptador adaptador_3 (
    .C2_Y(decodificador_c2_3_y), .C2_X(decodificador_c2_3_x), .C2_W(decodificador_c2_3_w),
    .C2_V(decodificador_c2_3_v), .C2_U(decodificador_c2_3_u), .C2_T(decodificador_c2_3_t),
    .C2_S(decodificador_c2_3_s), .SiM_Y(decodificador_sim_3_y), .SiM_X(decodificador_sim_3_x),
    .SiM_W(decodificador_sim_3_w), .SiM_V(decodificador_sim_3_v), .SiM_U(decodificador_sim_3_u),
    .SiM_T(decodificador_sim_3_t), .SiM_S(decodificador_sim_3_s), .Y(adaptador_3_y), .X(adaptador_3_x),
    .W(adaptador_3_w), .V(adaptador_3_v), .U(adaptador_3_u), .T(adaptador_3_t), .S(adaptador_3_s));
  Seven_Seg seven_seg_5 (.a(1'b0), .b(1'b0), .c(1'b0), .d(1'b0), .e(1'b0), .f(1'b0), .g(R2), .dp(1'b0));
  Seven_Seg seven_seg_6 (
    .a(adaptador_3_v), .b(adaptador_3_w), .c(adaptador_3_x), .d(adaptador_3_y), .e(adaptador_3_u),
    .f(adaptador_3_t), .g(adaptador_3_s), .dp(1'b0));

  // Other names for the same wires on the sheet: A = A2; B = B2

  // Notes on the sheet:
  //   A
  //   B
endmodule

/* Test case Test Carlos Guerrero:
Op Codi A2 A1 A0 B2 B1 B0 O C R2 R1 R0
#   0+0=0
0 0 0 0 0 0 0 0 0 X 0 0 0
#   0+1=1
0 0 0 0 0 0 0 1 0 X 0 0 1
#   0+2=2
0 0 0 0 0 0 1 0 0 X 0 1 0
#   0+3=3
0 0 0 0 0 0 1 1 0 X 0 1 1
#   0+-4=-4
0 0 0 0 0 1 0 0 0 X 1 0 0
#   0+-3=-3
0 0 0 0 0 1 0 1 0 X 1 0 1
#   0+-2=-2
0 0 0 0 0 1 1 0 0 X 1 1 0
#   0+-1=-1
0 0 0 0 0 1 1 1 0 X 1 1 1
#   1+0=1
0 0 0 0 1 0 0 0 0 X 0 0 1
#   1+1=2
0 0 0 0 1 0 0 1 0 X 0 1 0
#   1+2=3
0 0 0 0 1 0 1 0 0 X 0 1 1
#   1+3=4
0 0 0 0 1 0 1 1 1 X X X X
#   1+-4=-3
0 0 0 0 1 1 0 0 0 X 1 0 1
#   1+-3=-2
0 0 0 0 1 1 0 1 0 X 1 1 0
#   1+-2=-1
0 0 0 0 1 1 1 0 0 X 1 1 1
#   1+-1=0
0 0 0 0 1 1 1 1 0 X 0 0 0
#   2+0=2
0 0 0 1 0 0 0 0 0 X 0 1 0
#   2+1=3
0 0 0 1 0 0 0 1 0 X 0 1 1
#   2+2=4
0 0 0 1 0 0 1 0 1 X X X X
#   2+3=5
0 0 0 1 0 0 1 1 1 X X X X
#   2+-4=-2
0 0 0 1 0 1 0 0 0 X 1 1 0
#   2+-3=-1
0 0 0 1 0 1 0 1 0 X 1 1 1
#   2+-2=0
0 0 0 1 0 1 1 0 0 X 0 0 0
#   2+-1=1
0 0 0 1 0 1 1 1 0 X 0 0 1
#   3+0=3
0 0 0 1 1 0 0 0 0 X 0 1 1
#   3+1=4
0 0 0 1 1 0 0 1 1 X X X X
#   3+2=5
0 0 0 1 1 0 1 0 1 X X X X
#   3+3=6
0 0 0 1 1 0 1 1 1 X X X X
#   3+-4=-1
0 0 0 1 1 1 0 0 0 X 1 1 1
#   3+-3=0
0 0 0 1 1 1 0 1 0 X 0 0 0
#   3+-2=1
0 0 0 1 1 1 1 0 0 X 0 0 1
#   3+-1=2
0 0 0 1 1 1 1 1 0 X 0 1 0
#   -4+0=-4
0 0 1 0 0 0 0 0 0 X 1 0 0
#   -4+1=-3
0 0 1 0 0 0 0 1 0 X 1 0 1
#   -4+2=-2
0 0 1 0 0 0 1 0 0 X 1 1 0
#   -4+3=-1
0 0 1 0 0 0 1 1 0 X 1 1 1
#   -4+-4=-8
0 0 1 0 0 1 0 0 1 X X X X
#   -4+-3=-7
0 0 1 0 0 1 0 1 1 X X X X
#   -4+-2=-6
0 0 1 0 0 1 1 0 1 X X X X
#   -4+-1=-5
0 0 1 0 0 1 1 1 1 X X X X
#   -3+0=-3
0 0 1 0 1 0 0 0 0 X 1 0 1
#   -3+1=-2
0 0 1 0 1 0 0 1 0 X 1 1 0
#   -3+2=-1
0 0 1 0 1 0 1 0 0 X 1 1 1
#   -3+3=0
0 0 1 0 1 0 1 1 0 X 0 0 0
#   -3+-4=-7
0 0 1 0 1 1 0 0 1 X X X X
#   -3+-3=-6
0 0 1 0 1 1 0 1 1 X X X X
#   -3+-2=-5
0 0 1 0 1 1 1 0 1 X X X X
#   -3+-1=-4
0 0 1 0 1 1 1 1 0 X 1 0 0
#   -2+0=-2
0 0 1 1 0 0 0 0 0 X 1 1 0
#   -2+1=-1
0 0 1 1 0 0 0 1 0 X 1 1 1
#   -2+2=0
0 0 1 1 0 0 1 0 0 X 0 0 0
#   -2+3=1
0 0 1 1 0 0 1 1 0 X 0 0 1
#   -2+-4=-6
0 0 1 1 0 1 0 0 1 X X X X
#   -2+-3=-5
0 0 1 1 0 1 0 1 1 X X X X
#   -2+-2=-4
0 0 1 1 0 1 1 0 0 X 1 0 0
#   -2+-1=-3
0 0 1 1 0 1 1 1 0 X 1 0 1
#   -1+0=-1
0 0 1 1 1 0 0 0 0 X 1 1 1
#   -1+1=0
0 0 1 1 1 0 0 1 0 X 0 0 0
#   -1+2=1
0 0 1 1 1 0 1 0 0 X 0 0 1
#   -1+3=2
0 0 1 1 1 0 1 1 0 X 0 1 0
#   -1+-4=-5
0 0 1 1 1 1 0 0 1 X X X X
#   -1+-3=-4
0 0 1 1 1 1 0 1 0 X 1 0 0
#   -1+-2=-3
0 0 1 1 1 1 1 0 0 X 1 0 1
#   -1+-1=-2
0 0 1 1 1 1 1 1 0 X 1 1 0
#   0-0=0
1 0 0 0 0 0 0 0 0 X 0 0 0
#   0-1=-1
1 0 0 0 0 0 0 1 0 X 1 1 1
#   0-2=-2
1 0 0 0 0 0 1 0 0 X 1 1 0
#   0-3=-3
1 0 0 0 0 0 1 1 0 X 1 0 1
#   0--4=4
1 0 0 0 0 1 0 0 1 X X X X
#   0--3=3
1 0 0 0 0 1 0 1 0 X 0 1 1
#   0--2=2
1 0 0 0 0 1 1 0 0 X 0 1 0
#   0--1=1
1 0 0 0 0 1 1 1 0 X 0 0 1
#   1-0=1
1 0 0 0 1 0 0 0 0 X 0 0 1
#   1-1=0
1 0 0 0 1 0 0 1 0 X 0 0 0
#   1-2=-1
1 0 0 0 1 0 1 0 0 X 1 1 1
#   1-3=-2
1 0 0 0 1 0 1 1 0 X 1 1 0
#   1--4=5
1 0 0 0 1 1 0 0 1 X X X X
#   1--3=4
1 0 0 0 1 1 0 1 1 X X X X
#   1--2=3
1 0 0 0 1 1 1 0 0 X 0 1 1
#   1--1=2
1 0 0 0 1 1 1 1 0 X 0 1 0
#   2-0=2
1 0 0 1 0 0 0 0 0 X 0 1 0
#   2-1=1
1 0 0 1 0 0 0 1 0 X 0 0 1
#   2-2=0
1 0 0 1 0 0 1 0 0 X 0 0 0
#   2-3=-1
1 0 0 1 0 0 1 1 0 X 1 1 1
#   2--4=6
1 0 0 1 0 1 0 0 1 X X X X
#   2--3=5
1 0 0 1 0 1 0 1 1 X X X X
#   2--2=4
1 0 0 1 0 1 1 0 1 X X X X
#   2--1=3
1 0 0 1 0 1 1 1 0 X 0 1 1
#   3-0=3
1 0 0 1 1 0 0 0 0 X 0 1 1
#   3-1=2
1 0 0 1 1 0 0 1 0 X 0 1 0
#   3-2=1
1 0 0 1 1 0 1 0 0 X 0 0 1
#   3-3=0
1 0 0 1 1 0 1 1 0 X 0 0 0
#   3--4=7
1 0 0 1 1 1 0 0 1 X X X X
#   3--3=6
1 0 0 1 1 1 0 1 1 X X X X
#   3--2=5
1 0 0 1 1 1 1 0 1 X X X X
#   3--1=4
1 0 0 1 1 1 1 1 1 X X X X
#   -4-0=-4
1 0 1 0 0 0 0 0 0 X 1 0 0
#   -4-1=-5
1 0 1 0 0 0 0 1 1 X X X X
#   -4-2=-6
1 0 1 0 0 0 1 0 1 X X X X
#   -4-3=-7
1 0 1 0 0 0 1 1 1 X X X X
#   -4--4=0
1 0 1 0 0 1 0 0 0 X 0 0 0
#   -4--3=-1
1 0 1 0 0 1 0 1 0 X 1 1 1
#   -4--2=-2
1 0 1 0 0 1 1 0 0 X 1 1 0
#   -4--1=-3
1 0 1 0 0 1 1 1 0 X 1 0 1
#   -3-0=-3
1 0 1 0 1 0 0 0 0 X 1 0 1
#   -3-1=-4
1 0 1 0 1 0 0 1 0 X 1 0 0
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*/
